# Fritzing sketch Circuit (saved by Fritzing 1.0.6)
circuit board: 8.46667cm x 5.64444cm
perfboards: 1

parts:
  E = Camdenboss CTB0158-2 [part_number=CTB0158-2 package=THT]
  C31 = Film/Foil Capacitor [capacitance=100nF voltage=35V package="10mm [THT, pp]"]
  R1 = Resistor [tolerance=±1% resistance=1k package="0805 [SMD]"]
  L2 = Inductor [inductance=1µH package="1206 [SMD]"]
  P = POT [knob_status=50% power=0.5W package=pot_alpha_rv16af-20]
  R2 = Resistor [tolerance=±1% resistance=1k package="0805 [SMD]"]
  L1 = Inductor [inductance=10µH package="400 mil [THT]"]
  M = Basic FET P-Channel [package="TO220 [THT]"]
  C21 = Capacitor [package=cap-pth-5mm]
  C1 = Film/Foil Capacitor [capacitance=100nF voltage=35V package="5mm [THT, pp]"]
  C23 = Capacitor [package=cap-pth-5mm]
  C22 = Capacitor [package=cap-pth-5mm]
  C2 = Capacitor [package=cap-pth-5mm]
  C3 = Film/Foil Capacitor [capacitance=100nF voltage=35V package="10mm [THT, pp]"]

nets (from the pcb view):
  N1: E.pin1, C31.+, P.A, M.source, C1.-, C3.+
  N2: E.pin2, R1.Pin_1, L1.pin_1, C1.+
  N3: C31.-, P.S, R2.Pin_0, R2.Pin_1, M.gate, C21.2, C23.2, C22.2, C2.2, C3.-
  N4: R1.Pin_0, P.E
  N5: L2.pin_0, L1.pin_0, M.drain
  N6: L2.pin_1, C21.1, C23.1, C22.1, C2.1

notes:
  FET-D:K14
  L1-D:L19
  E-B:U32
